# Fritzing sketch lcd_wiring (saved by Fritzing 0.9.9b)
breadboards: 1

parts:
  Mod1 = Heltec WiFi LoRa 32 V2 [part_number=HTIT-WB32LA]
  DHT1 = DHT11 Humitidy and Temperature Sensor
  LCD2004-I2C1 = LCD2004-I2C
  Part1 = I2C level shifter bidirectional

nets (from the schematic view):
  N1: Mod1.pin_4, DHT1.DATA
  N2: Mod1.pin_16, Mod1.pin_17, DHT1.VDD, Part1.LV
  GND: Mod1.GND, DHT1.GND, LCD2004-I2C1.GND, Part1.GND
  N3: Mod1.pin_20, LCD2004-I2C1.VCC, Part1.HV
  N4: Mod1.pin_21, Mod1.pin_22
  N5: Mod1.pin_28, Part1.LV4
  N6: Mod1.pin_30, Part1.LV3
  N7: LCD2004-I2C1.SDA, Part1.HV4
  N8: LCD2004-I2C1.SCL, Part1.HV3

notes:
  Touch 9, 8, 7, 4

custom parts:
  DHT11 Humitidy and Temperature Sensor: DHT11 Humidity and Temperature Sensor
  LCD2004-I2C: A standard character display with 4x20 characters. Comes in many colors with LCM2004 IIC attached.
